// Digital circuit SOP.dig as structural Verilog
module SOP (
  input  A,
  input  C,
  input  B,
  input  D,
  output Y
);

  wire and_1_out, and_2_out, not_1_out, not_2_out;

  not not_1 (not_1_out, A);
  not not_2 (not_2_out, D);
  and and_1 (and_1_out, A, not_2_out);
  and and_2 (and_2_out, not_1_out, D);
  or or_1 (Y, and_1_out, and_2_out);
endmodule
